# Fritzing sketch Breadboard View (saved by Fritzing 0.9.3b)

parts:
  Part1 = AF_mshield-v1.2_breadboard
  Part2 = Arduino Mega 2560 (Rev3)
  M1 = DC Motor
  M2 = DC Motor
  M3 = DC Motor
  M4 = DC Motor
  VCC1 = Battery
  hc-sr1 = hc-sr04
  M5 = fc-51 [package=THT]
  M6 = fc-51 [package=THT]
  Part3 = RFID-RC522-v2
  J1 = Basic Servo

nets:
  N1: Part1.V+, VCC1.+
  GND: Part1.GND, Part2.GND, VCC1.-, hc-sr1.GND, M5.pin2, M6.pin2, Part3.GND, J1.gnd
  N2: Part1.3#89, Part2.D2_PWM
  N3: Part1.PWM2B, Part2.D3_PWM
  N4: Part1.DIR_CLK, Part2.D4_PWM
  N5: Part1.PWM0B, Part2.D5_PWM
  N6: Part1.PWM0A, Part2.D6_PWM
  N7: Part1.DIR_EN, Part2.D7_PWM
  N8: Part1.DIR_SER, Part2.D8_PWM
  N9: Part1.PWM1A, Part2.D9_PWM
  N10: Part1.PWM1B, Part2.D10_PWM, J1.pulse
  N11: Part1.PWM2A, Part2.D11_PWM
  N12: Part1.DIR_LATCH, Part2.D12_PWM
  N13: Part1.RESET, Part2.RESET
  VCC: Part1.VCC, Part2.5V, hc-sr1.VCC, M5.pin3, M6.pin3, J1.vcc
  9V: Part1.9V, Part2.VIN
  N14: Part1.1, Part2.A0, M5.pin1
  N15: Part1.2, Part2.A1, hc-sr1.Echo
  N16: Part1.3#111, Part2.A2
  N17: Part1.4, Part2.A3, hc-sr1.Trig
  N18: Part1.5, Part2.A4
  N19: Part1.6, Part2.A5, M6.pin1
  N20: Part1.P1#166, M1.pin_2
  N21: Part1.P2#167, M1.pin_1
  N22: Part1.P4#169, M3.pin_2
  N23: Part1.P5#170, M3.pin_1
  N24: Part1.P1#171, M4.pin_1
  N25: Part1.P2#172, M4.pin_2
  N26: Part1.P4#174, M2.pin_1
  N27: Part1.P5#175, M2.pin_2
  3V3: Part2.3V3, Part3.3.3V
  N28: Part2.D49, Part3.RST
  N29: Part2.D50, Part3.MISO
  N30: Part2.D51, Part3.MOSI
  N31: Part2.D52, Part3.SCK
  N32: Part2.D53, Part3.SDA

custom parts:
  : motor Shield v1 Adafruit Adafruit Motor/Stepper/Servo Shield for Arduino kit [v1.2] : ID 81 : $19.50 : Adafruit Industries, Unique & fun DIY electronics and kits
  RFID-RC522-v2: A simple China made RFID-RC522 Reader; do check the pin labels, as this is a MFRC522 based clone.
